# Fritzing sketch Baromalarm (saved by Fritzing 0.9.0b)

parts:
  Part1 = Barometric Pressure Sensor - BMP085 Breakout
  Arduino1 = Arduino Mini (Rev5)
  J1 = Piezo Speaker
  Part2 = NCP1400 Step-Up Breakout
  7SEG1 = 7-Segment LED I2C Backpack (blue)
  VCC1 = 4 x AAA Battery Mount

nets:
  VCC: Part1.VCC, Arduino1.5V, Part2.VOUT, 7SEG1.V+
  N1: Part1.SCL, Arduino1.A5
  N2: Part1.SDA, Arduino1.A4
  N3: Arduino1.D4, J1.pin2
  N4: Arduino1.D5_PWM, 7SEG1.SCL
  GND: Arduino1.GND, Part2.GND
  N5: J1.pin1, 7SEG1.GND
  N6: Part2.VIN, VCC1.+

custom parts:
  7-Segment LED I2C Backpack (blue): 4-digit, 7-segment LED Display with I2C Control
